# Fritzing sketch Hardware (saved by Fritzing 0.9.5d)
breadboards: 2

parts:
  Part1 = Arduino Uno (Rev3)
  U1 = LCD-16X2 [package=lcd-16x2]
  HC-SR04_Sensor_1 = HC-SR04 Ultrasonic Distance Sensor
  U2 = POT [package=alps_pot]
  LED1 = LED - 5mm [color="Red (633nm)" package="5 mm [THT]"]
  R1 = Resistor [tolerance=±5% resistance=220 package="0805 [SMD]"]
  J1 = Piezo Speaker

nets:
  N1: Part1.D9_PWM, HC-SR04_Sensor_1.TRIG
  N2: Part1.D10_PWM/SS, HC-SR04_Sensor_1.ECHO
  N3: Part1.D11_PWM/MOSI, U1.E
  N4: Part1.D12/MISO, U1.RS
  GND: Part1.GND, U1.VSS, U1.R_W, U1.K, HC-SR04_Sensor_1.GND, U2.A, LED1.anode, J1.pin1
  N5: Part1.D2, U1.DB7
  N6: Part1.D3_PWM, U1.DB6
  N7: Part1.D4, U1.DB5
  N8: Part1.D5_PWM, U1.DB4
  N9: Part1.D6_PWM, J1.pin2
  N10: Part1.D7, R1.Pin_0
  5V: Part1.5V, U1.VDD, U1.A, HC-SR04_Sensor_1.VCC, U2.E
  N11: U1.VO, U2.S
  N12: LED1.cathode, R1.Pin_1
